// Logisim project Feux_signal.circ as structural Verilog
module Feux_signalisation (
  output V_V,
  output V_O,
  output V_R,
  output P_V,
  output P_R
);

  wire and_1_out, and_2_out, and_3_out, and_4_out, and_5_out, and_6_out, and_7_out, and_8_out, and_9_out,
       and_10_out, and_11_out, clock_1_out, j_k_ff_1_q, j_k_ff_1_qn, j_k_ff_2_q, j_k_ff_2_qn, j_k_ff_3_q,
       j_k_ff_3_qn, j_k_ff_4_qn, not_1_out, not_2_out, not_3_out, not_4_out, not_5_out, not_6_out, not_7_out,
       not_8_out, not_9_out, not_10_out, not_11_out, not_12_out, not_13_out;

  Clock clock_1 (.out(clock_1_out));
  J_K_Flip_Flop j_k_ff_1 (
    .J(1'b1), .clk(clock_1_out), .K(1'b1), .Q(j_k_ff_1_q), .Qn(j_k_ff_1_qn));  // open: preset, en, reset
  J_K_Flip_Flop j_k_ff_2 (
    .J(1'b1), .clk(j_k_ff_1_q), .K(1'b1), .Q(j_k_ff_2_q), .Qn(j_k_ff_2_qn));  // open: preset, en, reset
  J_K_Flip_Flop j_k_ff_3 (
    .J(1'b1), .clk(j_k_ff_2_q), .K(1'b1), .Q(j_k_ff_3_q), .Qn(j_k_ff_3_qn));  // open: preset, en, reset
  J_K_Flip_Flop j_k_ff_4 (.J(1'b1), .clk(j_k_ff_3_q), .K(1'b1), .Qn(j_k_ff_4_qn));  // open: Q, preset, en, reset
  not not_1 (not_1_out, j_k_ff_4_qn);
  not not_2 (not_2_out, j_k_ff_3_qn);
  not not_3 (not_3_out, j_k_ff_4_qn);
  not not_4 (not_4_out, j_k_ff_2_qn);
  not not_5 (not_5_out, j_k_ff_4_qn);
  not not_6 (not_6_out, j_k_ff_3_qn);
  not not_7 (not_7_out, j_k_ff_2_qn);
  and and_1 (and_1_out, j_k_ff_4_qn, j_k_ff_2_qn);
  and and_2 (and_2_out, j_k_ff_4_qn, j_k_ff_3_qn);
  not not_8 (not_8_out, j_k_ff_3_qn);
  not not_9 (not_9_out, j_k_ff_2_qn);
  not not_10 (not_10_out, j_k_ff_1_qn);
  not not_11 (not_11_out, j_k_ff_3_qn);
  not not_12 (not_12_out, j_k_ff_2_qn);
  and and_3 (and_3_out, not_1_out, not_2_out);
  and and_4 (and_4_out, not_3_out, not_4_out);
  and and_5 (and_5_out, not_5_out, j_k_ff_3_qn, j_k_ff_2_qn);
  and and_6 (and_6_out, j_k_ff_4_qn, not_6_out, not_7_out);
  or or_1 (V_R, and_1_out, and_2_out);
  and and_7 (and_7_out, j_k_ff_4_qn, not_8_out, j_k_ff_2_qn);
  and and_8 (and_8_out, j_k_ff_4_qn, j_k_ff_3_qn, not_9_out);
  and and_9 (and_9_out, j_k_ff_4_qn, j_k_ff_3_qn, not_10_out);
  not not_13 (not_13_out, j_k_ff_4_qn);
  and and_10 (and_10_out, not_11_out, not_12_out);
  and and_11 (and_11_out, j_k_ff_3_qn, j_k_ff_2_qn, j_k_ff_1_qn);
  or or_2 (V_V, and_3_out, and_4_out);
  or or_3 (V_O, and_5_out, and_6_out);
  or or_4 (P_V, and_7_out, and_8_out, and_9_out);
  or or_5 (P_R, not_13_out, and_10_out, and_11_out);
endmodule

module Feux_sig (
  input  C3,
  input  C2,
  input  C1,
  input  C0,
  output V_V,
  output V_O,
  output V_R,
  output P_V,
  output P_R
);

  wire and_1_out, and_2_out, and_3_out, and_4_out, and_5_out, and_6_out, and_7_out, and_8_out, and_9_out,
       and_10_out, and_11_out, not_1_out, not_2_out, not_3_out, not_4_out, not_5_out, not_6_out, not_7_out,
       not_8_out, not_9_out, not_10_out, not_11_out, not_12_out, not_13_out;

  not not_1 (not_1_out, C3);
  and and_1 (and_1_out, not_1_out, not_2_out);
  not not_2 (not_2_out, C2);
  not not_3 (not_3_out, C3);
  and and_2 (and_2_out, not_3_out, not_4_out);
  not not_4 (not_4_out, C1);
  not not_5 (not_5_out, C3);
  and and_3 (and_3_out, not_5_out, C2, C1);
  not not_6 (not_6_out, C2);
  and and_4 (and_4_out, C3, not_6_out, not_7_out);
  not not_7 (not_7_out, C1);
  and and_5 (and_5_out, C3, C1);
  and and_6 (and_6_out, C3, C2);
  not not_8 (not_8_out, C2);
  and and_7 (and_7_out, C3, not_8_out, C1);
  and and_8 (and_8_out, C3, C2, not_9_out);
  not not_9 (not_9_out, C1);
  and and_9 (and_9_out, C3, C2, not_10_out);
  not not_10 (not_10_out, C0);
  not not_11 (not_11_out, C3);
  not not_12 (not_12_out, C2);
  and and_10 (and_10_out, not_12_out, not_13_out);
  not not_13 (not_13_out, C1);
  and and_11 (and_11_out, C2, C1, C0);
  or or_1 (V_V, and_1_out, and_2_out);
  or or_2 (V_O, and_3_out, and_4_out);
  or or_3 (V_R, and_5_out, and_6_out);
  or or_4 (P_V, and_7_out, and_8_out, and_9_out);
  or or_5 (P_R, not_11_out, and_10_out, and_11_out);
endmodule
