// Logisim project 4b_7segment_logisim.circ as structural Verilog
module de0_7_segment (
  input  D3,
  input  D2,
  input  D1,
  input  D0,
  output DP,
  output HEX6,
  output HEX5,
  output HEX4,
  output HEX3,
  output HEX2,
  output HEX1,
  output HEX0
);

  wire and_1_out, and_2_out, and_3_out, and_4_out, and_5_out, and_6_out, and_7_out, and_8_out, and_9_out,
       and_10_out, and_11_out, and_12_out, and_13_out, and_14_out, and_15_out, and_16_out, and_17_out,
       and_18_out, and_19_out, and_20_out, and_21_out, and_22_out, and_23_out, and_24_out, and_25_out,
       not_1_out, not_2_out, not_3_out, not_4_out, not_5_out, not_6_out, not_7_out, not_8_out, not_9_out,
       not_10_out, not_11_out, not_12_out, not_13_out, not_14_out, not_15_out, not_16_out, not_17_out,
       not_18_out, not_19_out, not_20_out, not_21_out, not_22_out, not_23_out, not_24_out, not_25_out,
       not_26_out, not_27_out, not_28_out, not_29_out, not_30_out, not_31_out, not_32_out, not_33_out,
       not_34_out, not_35_out, not_36_out, not_37_out, not_38_out, not_39_out, not_40_out, not_41_out;

  not not_1 (not_1_out, D3);
  not not_2 (not_2_out, D2);
  not not_3 (not_3_out, D1);
  not not_4 (not_4_out, D3);
  not not_5 (not_5_out, D1);
  not not_6 (not_6_out, D0);
  not not_7 (not_7_out, D3);
  not not_8 (not_8_out, D2);
  not not_9 (not_9_out, D3);
  not not_10 (not_10_out, D2);
  not not_11 (not_11_out, D3);
  not not_12 (not_12_out, D1);
  not not_13 (not_13_out, D3);
  and and_1 (and_1_out, not_13_out, D0);
  not not_14 (not_14_out, D2);
  not not_15 (not_15_out, D1);
  and and_2 (and_2_out, not_14_out, not_15_out, D0);
  not not_16 (not_16_out, D3);
  and and_3 (and_3_out, not_16_out, D2, not_17_out);
  not not_17 (not_17_out, D1);
  not not_18 (not_18_out, D3);
  not not_19 (not_19_out, D2);
  not not_20 (not_20_out, D1);
  not not_21 (not_21_out, D3);
  not not_22 (not_22_out, D1);
  not not_23 (not_23_out, D0);
  not not_24 (not_24_out, D2);
  not not_25 (not_25_out, D0);
  not not_26 (not_26_out, D3);
  not not_27 (not_27_out, D2);
  not not_28 (not_28_out, D0);
  not not_29 (not_29_out, D0);
  not not_30 (not_30_out, D3);
  not not_31 (not_31_out, D1);
  not not_32 (not_32_out, D0);
  not not_33 (not_33_out, D0);
  not not_34 (not_34_out, D3);
  not not_35 (not_35_out, D2);
  not not_36 (not_36_out, D1);
  not not_37 (not_37_out, D3);
  not not_38 (not_38_out, D1);
  not not_39 (not_39_out, D0);
  not not_40 (not_40_out, D2);
  not not_41 (not_41_out, D1);
  and and_4 (and_4_out, not_1_out, not_2_out, not_3_out);
  and and_5 (and_5_out, not_4_out, D2, D1, D0);
  or or_1 (HEX6, and_4_out, and_5_out, and_6_out);
  and and_6 (and_6_out, D3, D2, not_5_out, not_6_out);
  and and_7 (and_7_out, not_7_out, not_8_out, D0);
  and and_8 (and_8_out, not_9_out, not_10_out, D1);
  and and_9 (and_9_out, not_11_out, D1, D0);
  and and_10 (and_10_out, D3, D2, not_12_out, D0);
  or or_2 (HEX4, and_1_out, and_2_out, and_3_out);
  and and_11 (and_11_out, not_18_out, not_19_out, not_20_out, D0);
  and and_12 (and_12_out, not_21_out, D2, not_22_out, not_23_out);
  and and_13 (and_13_out, D2, D1, D0);
  and and_14 (and_14_out, D3, not_24_out, D1, not_25_out);
  and and_15 (and_15_out, not_26_out, not_27_out, D1, not_28_out);
  and and_16 (and_16_out, D3, D2, not_29_out);
  or or_3 (HEX2, and_15_out, and_16_out, and_17_out);
  and and_17 (and_17_out, D3, D2, D1);
  and and_18 (and_18_out, not_30_out, D2, not_31_out, D0);
  and and_19 (and_19_out, D2, D1, not_32_out);
  and and_20 (and_20_out, D3, D1, D0);
  and and_21 (and_21_out, D3, D2, not_33_out);
  and and_22 (and_22_out, not_34_out, not_35_out, not_36_out, D0);
  and and_23 (and_23_out, not_37_out, D2, not_38_out, not_39_out);
  and and_24 (and_24_out, D3, not_40_out, D1, D0);
  and and_25 (and_25_out, D3, D2, not_41_out, D0);
  or or_4 (HEX5, and_7_out, and_8_out, and_9_out, and_10_out);
  or or_5 (HEX3, and_11_out, and_12_out, and_13_out, and_14_out);
  or or_6 (HEX1, and_18_out, and_19_out, and_20_out, and_21_out);
  or or_7 (HEX0, and_22_out, and_23_out, and_24_out, and_25_out);

  assign DP = 1'b1;
endmodule
